# Fritzing sketch plotclock_shield (saved by Fritzing 0.9.3b)
circuit board: 4.2cm x 5.3cm
breadboards: 1

parts:
  Bauteil1 = Arduino Uno (Rev3)
  RIGHT = Basic Servo
  LEFT = Basic Servo
  LIFT = Basic Servo
  R1 = Resistor [tolerance=±5% resistance=220 package=THT]
  +_- = female pin header, 2 pins [form="♀ (female)"]
  RTC = female pin header, 4 pins [form="♀ (female)"]

nets:
  N1: Bauteil1.A4/SDA, RTC.pin2
  N2: Bauteil1.A5/SCL, RTC.pin1
  N3: Bauteil1.D2, RIGHT.pulse
  N4: Bauteil1.D3_PWM, LEFT.pulse
  N5: Bauteil1.D4, LIFT.pulse
  N6: Bauteil1.D5_PWM, R1.Pin_0
  VCC: Bauteil1.5V, RIGHT.vcc, LEFT.vcc, LIFT.vcc, RTC.pin3
  GND: Bauteil1.GND, RIGHT.gnd, LEFT.gnd, LIFT.gnd, +_-.pin2, RTC.pin4
  N7: R1.Pin_1, +_-.pin1

notes:
  GND
  5V
  SCA
  SCL
  D + -
  LED
  github.com/drayde/plotclock
